# Fritzing sketch circuit_diagram (saved by Fritzing 0.9.3b)
circuit board: 8.46667cm x 5.64444cm
breadboards: 1

parts:
  Arduino_Nano = Arduino Nano (Rev3.0)
  Buzzer = Piezo Speaker
  Temp_Sensor = TMP36 [package=to-92]
  Warning_LED = LED - 5mm [color="Red (633nm)" package="5 mm [THT]"]
  LED_Resistor = Resistor [tolerance=±5% resistance=220 package=THT]

nets:
  GND: Arduino_Nano.GND, Buzzer.pin1, Temp_Sensor.GND, Warning_LED.cathode
  N1: Arduino_Nano.D2, LED_Resistor.Pin_1
  N2: Arduino_Nano.D3, Buzzer.pin2
  N3: Arduino_Nano.A1, Temp_Sensor.VOUT
  3V3: Arduino_Nano.AREF, Arduino_Nano.3V3, Temp_Sensor.VCC
  N4: Warning_LED.anode, LED_Resistor.Pin_0
